# Fritzing sketch BrewTemp (saved by Fritzing 0.9.3b)
breadboards: 1

parts:
  WeMos_D1_Mini1 = WeMos D1 Mini  # not connected
  DS1 = DS18B20 1-Wire Temperature Sensor [part_number=DS18B20]
  DS2 = DS18B20 1-Wire Temperature Sensor [part_number=DS18B20]
  R2 = Resistor [tolerance=±5% resistance=4.7k package=THT]
  R1 = Resistor [tolerance=±5% resistance=4.7k package=THT]
  LED1 = LED - 5mm [color="Green (555nm)" package="5 mm [THT]"]
  LED2 = LED - 5mm [color="Red (633nm)" package="5 mm [THT]"]
  LED3 = LED - 5mm [color="Blue (470nm)" package="5 mm [THT]"]
  R3 = Resistor [tolerance=±5% resistance=330 package=THT]  # not connected
  R4 = Resistor [tolerance=±5% resistance=330 package=THT]
  R5 = Resistor [tolerance=±5% resistance=330 package=THT]
  U1 = 2-Channel 5v Relay Shield [package=relay-2ch5v10a]
  Reset = Round Pushbutton

nets:
  GND: DS1.GND, DS2.GND, U1.GND, Reset.leg1
  N1: DS1.DQ, R2.Pin_0
  VDD: DS1.VDD, DS2.VDD, R2.Pin_1, R1.Pin_1, LED1.anode, LED2.anode, LED3.anode, U1.VCC
  N2: DS2.DQ, R1.Pin_0
  N3: R4.Pin_0, U1.IN1
  N4: R5.Pin_0, U1.IN2

notes:
  Sensor Fermentador
  Sensor Congelador
  R1 - 4K7 Ω
  R2 - 4K7 Ω
  R3 - 330 Ω
  R4 - 330 Ω
  R5 - 330 Ω
  Activo 220 VAC - CALEFACTOR
  Activo 220 VAC - CONGELADOR

custom parts:
  2-Channel 5v Relay Shield: 2 Channel 5v Relay Shield w. 2x SPD-06VDC-SD-C
